# Fritzing sketch random_LED (saved by Fritzing 0.9.3b)
breadboards: 1

parts:
  부품1 = Arduino Uno (Rev3)
  LED1 = LED - 5mm [color="White (4500K)" package="5 mm [THT]"]
  LED2 = LED - 5mm [color="White (4500K)" package="5 mm [THT]"]
  LED3 = LED - 5mm [color="White (4500K)" package="5 mm [THT]"]
  S1 = Momentary Switch [package=ksa_sealed_tac_switch]
  R1 = Resistor [tolerance=±5% resistance=10k package=THT]
  R2 = Resistor [tolerance=±5% resistance=220 package=THT]
  R3 = Resistor [tolerance=±5% resistance=220 package=THT]
  R4 = Resistor [tolerance=±5% resistance=220 package=THT]

nets:
  N1: 부품1.D8, S1.1
  N2: 부품1.GND, LED1.cathode, LED2.cathode, LED3.cathode, R1.Pin_1
  N3: 부품1.D2, R4.Pin_1
  N4: 부품1.D3_PWM, R3.Pin_1
  N5: 부품1.D4, R2.Pin_1
  N6: 부품1.5V, S1.4
  N7: LED1.anode, R4.Pin_0
  N8: LED2.anode, R3.Pin_0
  N9: LED3.anode, R2.Pin_0
  N10: S1.2, R1.Pin_0
