# Fritzing sketch rgbLED_rainbow (saved by Fritzing 0.9.3b)
breadboards: 1

parts:
  부품1 = Arduino Uno (Rev3)
  LED1 = RGB LED (com. cathode, rgb) [package="5 mm [THT]"]
  R1 = Rotary Potentiometer (Small) [maximum_resistance=10kΩ package=THT]

nets:
  N1: 부품1.D9_PWM, LED1.red_anode
  N2: 부품1.D10_PWM/SS, LED1.green_anode
  N3: 부품1.D11_PWM/MOSI, LED1.blue_anode
  N4: 부품1.5V, R1.leg2
  N5: 부품1.GND, R1.leg1
  N6: LED1.common_cathode, R1.wiper
